// Logisim project sdp_export.circ as structural Verilog: 2 circuits, main circuit SDP_uclk_writefirst_mk0
module SDP_uclk_writefirst_mk0 (
  input  [3:0] WR_ADDR,
  input  [3:0] A_RD_ADDR,
  input  RAMCLK,
  input  WE,
  input  [3:0] B_RD_ADDR,
  input  [3:0] DIN,
  input  RAMCLR,
  output [3:0] AOUT,
  output [3:0] BOUT,
  output WR_CYCLE
);

  wire counter_1_carry, CYCLE_1, WE_Cycle_0;
  wire [3:0] multiplexer_1_out, multiplexer_2_out, ram_1_dout, ram_2_dout;

  and and_1 (WE_Cycle_0, WR_CYCLE, WE);
  Counter #(.max('h1), .width(1)) counter_1 (
    .clr(RAMCLR), .load(1'b0), .up(1'b1), .count(1'b1), .clk(RAMCLK), .carry(counter_1_carry));  // open: D, Q
  Multiplexer #(.enable("false"), .width(4)) multiplexer_1 (
    .in0(WR_ADDR), .in1(A_RD_ADDR), .out(multiplexer_1_out), .sel(CYCLE_1));
  Multiplexer #(.enable("false"), .width(4)) multiplexer_2 (
    .in0(WR_ADDR), .in1(B_RD_ADDR), .out(multiplexer_2_out), .sel(CYCLE_1));
  RAM #(.addrWidth(4), .clearpin("true"), .dataWidth(4), .enables("line")) ram_1 (
    .addr(multiplexer_1_out), .we(WE_Cycle_0), .clk(RAMCLK), .din(DIN), .dout(ram_1_dout), .clr(RAMCLR));
  RAM #(.addrWidth(4), .clearpin("true"), .dataWidth(4), .enables("line")) ram_2 (
    .addr(multiplexer_2_out), .we(WE_Cycle_0), .clk(RAMCLK), .din(DIN), .dout(ram_2_dout), .clr(RAMCLR));
  Comparator #(.width(1)) comparator_1 (.a(1'b0), .b(counter_1_carry), .eq(WR_CYCLE));  // open: gt, lt
  Comparator #(.width(1)) comparator_2 (.a(1'b1), .b(counter_1_carry), .eq(CYCLE_1));  // open: gt, lt
  Register #(.width(4)) register_1 (.D(ram_1_dout), .en(CYCLE_1), .clk(RAMCLK), .Q(AOUT), .clr(RAMCLR));
  Register #(.width(4)) register_2 (.D(ram_2_dout), .en(CYCLE_1), .clk(RAMCLK), .Q(BOUT), .clr(RAMCLR));

  // Other names for the same wires on the sheet: CYCLE_0 = WR_CYCLE
endmodule

module SDP_tb (
  output [3:0] B_RD_ADDR,
  output [3:0] WR_ADDR,
  output [3:0] AOUT,
  output [3:0] A_RD_ADDR,
  output [3:0] BOUT,
  output WR_CYCLE,
  output [3:0] DIN,
  output SYSCLK,
  output [4:0] COUNT,
  output LT_16
);

  wire comparator_1_eq, comparator_1_lt, d_ff_1_q, RAMCLK, RAMCLR_out;

  Clock u_RAMCLK (.out(RAMCLK));
  D_Flip_Flop d_ff_1 (.D(SYSCLK), .clk(RAMCLK), .Q(d_ff_1_q));  // open: Qn, preset, reset
  not not_1 (SYSCLK, d_ff_1_q);
  Button RAMCLR (.out(RAMCLR_out));
  Counter #(.max('h1f), .width(5)) counter_1 (
    .clr(RAMCLR_out), .load(1'b0), .up(1'b1), .count(1'b1), .clk(SYSCLK), .Q({COUNT[4], A_RD_ADDR}));  // open: D, carry
  Subtractor #(.width(4)) subtractor_1 (.a(A_RD_ADDR), .b(4'b0001), .out(B_RD_ADDR));  // open: bin, bout
  SDP_uclk_writefirst_mk0 sdp_uclk_writefirst_mk0_1 (
    .WR_ADDR(A_RD_ADDR), .A_RD_ADDR(A_RD_ADDR), .RAMCLK(RAMCLK), .WE(LT_16), .B_RD_ADDR(B_RD_ADDR),
    .DIN(A_RD_ADDR), .RAMCLR(RAMCLR_out), .AOUT(AOUT), .BOUT(BOUT), .WR_CYCLE(WR_CYCLE));
  _7_Segment_Display u_7_segment_display_1 ();  // open: g, f, a, b, e, d, c, dp
  // BCD_to_7_Segment_decoder bcd_to_7_segment_decoder_1: pin names not known
  // Binary_to_BCD_converter #(.binvalue(5)) binary_to_bcd_converter_1: pin names not known; wires that end beside it: {COUNT[4], A_RD_ADDR}
  _7_Segment_Display u_7_segment_display_2 ();  // open: g, f, a, b, e, d, c, dp
  // BCD_to_7_Segment_decoder bcd_to_7_segment_decoder_2: pin names not known
  Comparator #(.mode("unsigned"), .width(5)) comparator_1 (
    .a({COUNT[4], A_RD_ADDR}), .b(5'b01111), .eq(comparator_1_eq), .lt(comparator_1_lt));  // open: gt
  or or_1 (LT_16, comparator_1_eq, comparator_1_lt);

  assign COUNT[3:0] = A_RD_ADDR;
  assign DIN = A_RD_ADDR;
  assign WR_ADDR = A_RD_ADDR;

  // Notes on the sheet:
  //   This simple test bench is driven by a counter. On cycles 0-15, ram(i)=i is written. The A port reads from COUNT(3 downto 0), port B reads from COUNT(3 downto 0) - 1.
endmodule
